# Fritzing sketch Kaylins_Robot (saved by Fritzing 0.9.0b)

parts:
  Raspberry_Pi1 = Raspberry Pi B rev2
  PWM1 = PCA9685 16x12-bit PWM Breakout
  M1 = DC Motor
  M2 = DC Motor
  J3 = Basic Servo
  Part2 = PowerBoost 500 Charger
  U1 = LIPO-2000mAh [package=lipo-2000]
  Power_plug1 = Power plug
  Part4 = SainSmart L298M Motor Driver

nets:
  N1: Raspberry_Pi1.3V3, PWM1.no_name_yet#505
  N2: Raspberry_Pi1.GPIO_2, PWM1.no_name_yet#504
  N3: Raspberry_Pi1.GPIO_3, PWM1.no_name_yet#503
  N4: Raspberry_Pi1.GND, PWM1.no_name_yet#501, PWM1.no_name_yet#1012
  N5: Raspberry_Pi1.GPIO_14, Part4.IN2
  N6: Raspberry_Pi1.GPIO_15, Part4.IN1
  N7: Raspberry_Pi1.GPIO_17, Part4.IN3
  GND: Raspberry_Pi1.GPIO_4, M1.pin_1, Power_plug1.GND, Part4.IN4, Part4.OUT4, Part4.GND
  N8: PWM1.no_name_yet#12, J3.pulse
  N9: M1.pin_2, Part4.OUT3
  N10: M2.pin_1, Part4.OUT2
  N11: M2.pin_2, Part4.OUT1
  N12: Part2.GND, U1.-
  N13: Part2.VBAT, U1.+
  VCC: Power_plug1.VCC, Part4.VCC

custom parts:
  PowerBoost 500 Charger: The PowerBoost 500C is a little DC/DC boost converter module that can be powered by any 3.7V LiIon/LiPoly battery, and convert the battery output to 5.2V DC for running your 5V projects. At its heart is a TPS61090 boost converter from TI. This boost converter chip has some really nice extras such as low battery detection, 2A internal switch, synchronous conversion, excellent efficiency, and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
